# Fritzing sketch layout (saved by Fritzing 0.6.5b)

parts:
  Arduino1 = Arduino
  Onderdeel1 = Arduino MP3 Player Shield  # not connected
  S2 = Round Pushbutton
  SPKR1 = Loudspeaker  # not connected

nets:
  N1: Arduino1.D2, S2.leg0
  N2: Arduino1.+5V, S2.leg1
